// Logisim project avtomat_var3.circ as structural Verilog: 1 circuit, main circuit avtomat_var3
module avtomat_var3 (
  input  x1,
  input  x2,
  input  C,
  input  R,
  output T1,
  output Q1,
  output T2,
  output Q2,
  output y1,
  output y2
);

  wire DD1_1_out, DD1_2_out, DD1_3_out, DD1_4_out, DD2_1_out, DD2_2_out, DD2_4_out, DD3_1_out, DD3_2_out,
       DD3_3_out, DD4_1_out, DD4_2_out, DD4_4_out, DD5_1_out, DD5_2_out, DD5_3_out, DD5_4_out, DD7_qn, DD8_qn;

  nor DD1_1 (DD1_1_out, x1, x1);
  nor DD1_2 (DD1_2_out, x2, x2);
  nor DD1_3 (DD1_3_out, Q1, x1);
  nor DD1_4 (DD1_4_out, DD7_qn, DD8_qn);
  nor DD2_4 (DD2_4_out, Q2, x2);
  nor DD3_1 (DD3_1_out, DD8_qn, DD1_2_out);
  nor DD4_1 (DD4_1_out, Q2, x1);
  nor DD4_2 (DD4_2_out, Q1, x2);
  nor DD4_4 (DD4_4_out, x1, DD1_2_out);
  nor DD5_1 (DD5_1_out, DD1_1_out, x2);
  nor DD5_2 (DD5_2_out, Q1, Q2);
  nor DD2_1 (DD2_1_out, DD1_3_out, x2);
  nor DD3_2 (DD3_2_out, DD2_4_out, x1);
  nor DD4_3 (y1, DD4_1_out, DD4_2_out);
  nor DD5_3 (DD5_3_out, DD4_4_out, DD5_1_out);
  nor DD2_2 (DD2_2_out, DD2_1_out, DD2_1_out);
  nor DD3_3 (DD3_3_out, DD3_2_out, DD3_2_out);
  nor DD5_4 (DD5_4_out, DD5_3_out, DD5_3_out);
  nor DD2_3 (T1, DD2_2_out, DD1_4_out);
  nor DD3_4 (T2, DD3_3_out, DD3_1_out);
  nor DD6_1 (y2, DD5_4_out, DD5_2_out);
  T_Flip_Flop #(.trigger("rising")) DD7 (.T(T1), .clk(C), .Q(Q1), .Qn(DD7_qn), .reset(R));  // open: preset
  T_Flip_Flop #(.trigger("rising")) DD8 (.T(T2), .clk(C), .Q(Q2), .Qn(DD8_qn), .reset(R));  // open: preset

  // Notes on the sheet:
  //   nx1
  //   x1
  //   x2
  //   nx2
  //   nQ1
  //   Q1
  //   Q2
  //   nQ2
  //   інвертори входів
  //   T1
  //   T2
  //   y1
  //   y2
endmodule
