// Logisim project probe_test.circ as structural Verilog: 1 circuit
module main (
);

  // NOR_Gate nor_1 is placed but not wired
  // NOR_Gate nor_2 is placed but not wired
  T_Flip_Flop t_ff_1 ();  // open: T, clk, Q, Qn, reset, preset
  T_Flip_Flop t_ff_2 ();  // open: clk, T, Q, Qn, preset, reset
endmodule
